// Logisim project prototype.circ as structural Verilog: 1 circuit, main circuit main
module main (
);

  wire and_1_out, and_3_out, button_1_out, cdm_8_mark5_1_p1, cdm_8_mark5_1_p2, cdm_8_mark5_1_p4,
       cdm_8_mark5_1_p5, cdm_8_mark5_1_p7, cdm_8_mark5_1_p8, cdm_8_mark5_1_p9, cdm_8_mark5_1_p10,
       cdm_8_mark5_1_p11, clock, code, data, decoder_2_out0, decoder_2_out1, decoder_2_out2, decoder_2_out3,
       decoder_3_out0, decoder_3_out1, decoder_3_out2, decoder_3_out3, decoder_3_out4, decoder_3_out5,
       decoder_3_out6, decoder_3_out7, decoder_3_out8, decoder_3_out9, decoder_3_out10, decoder_3_out11,
       decoder_3_out12, decoder_3_out13, decoder_3_out14, decoder_3_out15, decoder_3_out16, decoder_3_out17,
       decoder_3_out18, decoder_3_out19, decoder_3_out20, decoder_3_out21, decoder_3_out22, decoder_3_out23,
       decoder_3_out24, decoder_3_out25, decoder_3_out26, decoder_3_out27, decoder_3_out28, decoder_3_out29,
       decoder_3_out30, decoder_3_out31, not_1_out, not_2_out, not_3_out, read, video;
  wire [6:0] vaddr;
  wire [7:0] cdm_8_mark5_1_p14, cdm_8_mark5_1_p15, controlled_buffer_1_out, multiplexer_1_out,
       multiplexer_2_out, multiplexer_3_out, multiplexer_4_out, multiplexer_5_out, multiplexer_6_out,
       multiplexer_6_out_2, multiplexer_6_out_3, multiplexer_6_out_4;
  wire [7:7] adder_1_out;
  wire [15:0] cdm_8_mark5_1_p13;
  wire [31:0] demultiplexer_1_out0, demultiplexer_1_out1, multiplexer_7_out, multiplexer_8_out, row0, row1,
       row2, row3, row4, row5, row6, row7, row8, row9, row10, row11, row12, row13, row14, row15, row16,
       row17, row18, row19, row20, row21, row22, row23, row24, row25, row26, row27, row28, row29, row30,
       row31, wrow0, wrow1, wrow2, wrow3, wrow4, wrow5, wrow6, wrow7, wrow8, wrow9, wrow10, wrow11, wrow12,
       wrow13, wrow14, wrow15, wrow16, wrow17, wrow18, wrow19, wrow20, wrow21, wrow22, wrow23, wrow24,
       wrow25, wrow26, wrow27, wrow28, wrow29, wrow30, wrow31;

  // Probe on cdm_8_mark5_1_p1
  // Probe on cdm_8_mark5_1_p5
  // Probe on cdm_8_mark5_1_p4
  // Probe on cdm_8_mark5_1_p2
  Button button_1 (.out(button_1_out));
  Clock clock_1 (.out(clock));
  // Probe on cdm_8_mark5_1_p7
  // Probe on cdm_8_mark5_1_p9
  // Probe on cdm_8_mark5_1_p8
  // CdM_8_mark5 cdm_8_mark5_1: pin names not known; wires that end beside it: cdm_8_mark5_1_p1, cdm_8_mark5_1_p2, clock, cdm_8_mark5_1_p4, cdm_8_mark5_1_p5, button_1_out, cdm_8_mark5_1_p7, cdm_8_mark5_1_p8, cdm_8_mark5_1_p9, cdm_8_mark5_1_p10, cdm_8_mark5_1_p11, read, cdm_8_mark5_1_p13, cdm_8_mark5_1_p14, cdm_8_mark5_1_p15
  Decoder #(.disabled(0)) decoder_1 (.out0(code), .out1(data), .sel(cdm_8_mark5_1_p10), .en(cdm_8_mark5_1_p11));
  assign controlled_buffer_1_out = not_1_out ? cdm_8_mark5_1_p14 : 8'bz;  // Controlled_Buffer controlled_buffer_1
  not not_1 (not_1_out, read);
  assign cdm_8_mark5_1_p15 = read ? controlled_buffer_1_out : 8'bz;  // Controlled_Buffer controlled_buffer_2
  // Probe on cdm_8_mark5_1_p13
  // Probe on controlled_buffer_1_out
  // Probe on cdm_8_mark5_1_p13[7:0]
  Adder adder_1 (.a(cdm_8_mark5_1_p13[7:0]), .b(8'h20), .out({adder_1_out[7], vaddr}));  // open: cin, cout
  assign controlled_buffer_1_out = and_1_out ? multiplexer_1_out : 8'bz;  // Controlled_Buffer controlled_buffer_3
  and and_1 (and_1_out, video, read);
  // Probe on {adder_1_out[7], vaddr}
  not not_2 (not_2_out, read);
  ROM #(.addrWidth(16)) rom_1 (.addr(cdm_8_mark5_1_p13), .data(controlled_buffer_1_out), .sel(code));
  RAM #(.addrWidth(16)) ram_1 (
    .addr(cdm_8_mark5_1_p13), .data(controlled_buffer_1_out), .sel(data), .clk(clock), .ld(read));  // open: clr
  and and_2 (video, adder_1_out[7], data);
  Multiplexer #(.select(2), .width(8), .enable("false")) multiplexer_1 (
    .in0(multiplexer_6_out_4), .in1(multiplexer_6_out_3), .in2(multiplexer_6_out_2), .in3(multiplexer_6_out),
    .out(multiplexer_1_out), .sel(vaddr[1:0]));
  Decoder #(.select(2), .disabled(0)) decoder_2 (
    .out0(decoder_2_out0), .out1(decoder_2_out1), .out2(decoder_2_out2), .out3(decoder_2_out3),
    .sel(vaddr[1:0]), .en(not_2_out));
  Multiplexer #(.width(8), .enable("false")) multiplexer_2 (
    .in0(multiplexer_6_out_4), .in1(controlled_buffer_1_out), .out(multiplexer_2_out), .sel(decoder_2_out0));
  Multiplexer #(.width(8), .enable("false")) multiplexer_3 (
    .in0(multiplexer_6_out_3), .in1(controlled_buffer_1_out), .out(multiplexer_3_out), .sel(decoder_2_out1));
  Multiplexer #(.width(8), .enable("false")) multiplexer_4 (
    .in0(multiplexer_6_out_2), .in1(controlled_buffer_1_out), .out(multiplexer_4_out), .sel(decoder_2_out2));
  Multiplexer #(.width(8), .enable("false")) multiplexer_5 (
    .in0(multiplexer_6_out), .in1(controlled_buffer_1_out), .out(multiplexer_5_out), .sel(decoder_2_out3));
  Demultiplexer #(.width(32)) demultiplexer_1 (
    .out0(demultiplexer_1_out0), .out1(demultiplexer_1_out1),
    .in({multiplexer_2_out, multiplexer_3_out, multiplexer_4_out, multiplexer_5_out}), .sel(vaddr[6]),
    .en(not_2_out));
  Multiplexer #(.width(32), .enable("false")) multiplexer_6 (
    .in0(multiplexer_7_out), .in1(multiplexer_8_out),
    .out({multiplexer_6_out_4, multiplexer_6_out_3, multiplexer_6_out_2, multiplexer_6_out}), .sel(vaddr[6]));
  Multiplexer #(.select(4), .width(32), .enable("false")) multiplexer_7 (
    .in0(row0), .in1(row1), .in2(row2), .in3(row3), .in4(row4), .in5(row5), .in6(row6), .in7(row7),
    .in8(row8), .in9(row9), .in10(row10), .in11(row11), .in12(row12), .in13(row13), .in14(row14),
    .in15(row15), .out(multiplexer_7_out), .sel(vaddr[5:2]));
  Multiplexer #(.select(4), .width(32), .enable("false")) multiplexer_8 (
    .in0(row16), .in1(row17), .in2(row18), .in3(row19), .in4(row20), .in5(row21), .in6(row22), .in7(row23),
    .in8(row24), .in9(row25), .in10(row26), .in11(row27), .in12(row28), .in13(row29), .in14(row30),
    .in15(row31), .out(multiplexer_8_out), .sel(vaddr[5:2]));
  Demultiplexer #(.select(4), .width(32)) demultiplexer_2 (
    .out0(wrow0), .out1(wrow1), .out2(wrow2), .out3(wrow3), .out4(wrow4), .out5(wrow5), .out6(wrow6),
    .out7(wrow7), .out8(wrow8), .out9(wrow9), .out10(wrow10), .out11(wrow11), .out12(wrow12), .out13(wrow13),
    .out14(wrow14), .out15(wrow15), .in(demultiplexer_1_out0), .sel(vaddr[5:2]), .en(not_2_out));
  Demultiplexer #(.select(4), .width(32)) demultiplexer_3 (
    .out0(wrow16), .out1(wrow17), .out2(wrow18), .out3(wrow19), .out4(wrow20), .out5(wrow21), .out6(wrow22),
    .out7(wrow23), .out8(wrow24), .out9(wrow25), .out10(wrow26), .out11(wrow27), .out12(wrow28),
    .out13(wrow29), .out14(wrow30), .out15(wrow31), .in(demultiplexer_1_out1), .sel(vaddr[5:2]),
    .en(not_2_out));
  not not_3 (not_3_out, read);
  and and_3 (and_3_out, video, not_3_out);
  Decoder #(.select(5), .disabled(0)) decoder_3 (
    .out0(decoder_3_out0), .out1(decoder_3_out1), .out2(decoder_3_out2), .out3(decoder_3_out3),
    .out4(decoder_3_out4), .out5(decoder_3_out5), .out6(decoder_3_out6), .out7(decoder_3_out7),
    .out8(decoder_3_out8), .out9(decoder_3_out9), .out10(decoder_3_out10), .out11(decoder_3_out11),
    .out12(decoder_3_out12), .out13(decoder_3_out13), .out14(decoder_3_out14), .out15(decoder_3_out15),
    .out16(decoder_3_out16), .out17(decoder_3_out17), .out18(decoder_3_out18), .out19(decoder_3_out19),
    .out20(decoder_3_out20), .out21(decoder_3_out21), .out22(decoder_3_out22), .out23(decoder_3_out23),
    .out24(decoder_3_out24), .out25(decoder_3_out25), .out26(decoder_3_out26), .out27(decoder_3_out27),
    .out28(decoder_3_out28), .out29(decoder_3_out29), .out30(decoder_3_out30), .out31(decoder_3_out31),
    .sel(vaddr[6:2]), .en(and_3_out));
  Register #(.width(32)) register_1 (.D(wrow0), .en(decoder_3_out0), .Q(row0), .clk(clock));  // open: clr
  Register #(.width(32)) register_2 (.D(wrow1), .en(decoder_3_out1), .Q(row1), .clk(clock));  // open: clr
  Register #(.width(32)) register_3 (.D(wrow2), .en(decoder_3_out2), .Q(row2), .clk(clock));  // open: clr
  Register #(.width(32)) register_4 (.D(wrow3), .en(decoder_3_out3), .Q(row3), .clk(clock));  // open: clr
  Register #(.width(32)) register_5 (.D(wrow4), .en(decoder_3_out4), .Q(row4), .clk(clock));  // open: clr
  Register #(.width(32)) register_6 (.D(wrow5), .en(decoder_3_out5), .Q(row5), .clk(clock));  // open: clr
  Register #(.width(32)) register_7 (.D(wrow6), .en(decoder_3_out6), .Q(row6), .clk(clock));  // open: clr
  Register #(.width(32)) register_8 (.D(wrow7), .en(decoder_3_out7), .Q(row7), .clk(clock));  // open: clr
  Register #(.width(32)) register_9 (.D(wrow8), .en(decoder_3_out8), .Q(row8), .clk(clock));  // open: clr
  Register #(.width(32)) register_10 (.D(wrow9), .en(decoder_3_out9), .Q(row9), .clk(clock));  // open: clr
  Register #(.width(32)) register_11 (.D(wrow10), .en(decoder_3_out10), .Q(row10), .clk(clock));  // open: clr
  Register #(.width(32)) register_12 (.D(wrow11), .en(decoder_3_out11), .Q(row11), .clk(clock));  // open: clr
  Register #(.width(32)) register_13 (.D(wrow12), .en(decoder_3_out12), .Q(row12), .clk(clock));  // open: clr
  Register #(.width(32)) register_14 (.D(wrow13), .en(decoder_3_out13), .Q(row13), .clk(clock));  // open: clr
  Register #(.width(32)) register_15 (.D(wrow14), .en(decoder_3_out14), .Q(row14), .clk(clock));  // open: clr
  Register #(.width(32)) register_16 (.D(wrow15), .en(decoder_3_out15), .Q(row15), .clk(clock));  // open: clr
  Register #(.width(32)) register_17 (.D(wrow16), .en(decoder_3_out16), .Q(row16), .clk(clock));  // open: clr
  Register #(.width(32)) register_18 (.D(wrow17), .en(decoder_3_out17), .Q(row17), .clk(clock));  // open: clr
  Register #(.width(32)) register_19 (.D(wrow18), .en(decoder_3_out18), .Q(row18), .clk(clock));  // open: clr
  Register #(.width(32)) register_20 (.D(wrow19), .en(decoder_3_out19), .Q(row19), .clk(clock));  // open: clr
  Register #(.width(32)) register_21 (.D(wrow20), .en(decoder_3_out20), .Q(row20), .clk(clock));  // open: clr
  Register #(.width(32)) register_22 (.D(wrow21), .en(decoder_3_out21), .Q(row21), .clk(clock));  // open: clr
  Register #(.width(32)) register_23 (.D(wrow22), .en(decoder_3_out22), .Q(row22), .clk(clock));  // open: clr
  Register #(.width(32)) register_24 (.D(wrow23), .en(decoder_3_out23), .Q(row23), .clk(clock));  // open: clr
  Register #(.width(32)) register_25 (.D(wrow24), .en(decoder_3_out24), .Q(row24), .clk(clock));  // open: clr
  Register #(.width(32)) register_26 (.D(wrow25), .en(decoder_3_out25), .Q(row25), .clk(clock));  // open: clr
  Register #(.width(32)) register_27 (.D(wrow26), .en(decoder_3_out26), .Q(row26), .clk(clock));  // open: clr
  Register #(.width(32)) register_28 (.D(wrow27), .en(decoder_3_out27), .Q(row27), .clk(clock));  // open: clr
  Register #(.width(32)) register_29 (.D(wrow28), .en(decoder_3_out28), .Q(row28), .clk(clock));  // open: clr
  Register #(.width(32)) register_30 (.D(wrow29), .en(decoder_3_out29), .Q(row29), .clk(clock));  // open: clr
  Register #(.width(32)) register_31 (.D(wrow30), .en(decoder_3_out30), .Q(row30), .clk(clock));  // open: clr
  Register #(.width(32)) register_32 (.D(wrow31), .en(decoder_3_out31), .Q(row31), .clk(clock));  // open: clr
  DotMatrix #(.inputtype("row"), .matrixcols(32), .matrixrows(32)) dotmatrix_1 (
    .row0(row0), .row1(row1), .row2(row2), .row3(row3), .row4(row4), .row5(row5), .row6(row6), .row7(row7),
    .row8(row8), .row9(row9), .row10(row10), .row11(row11), .row12(row12), .row13(row13), .row14(row14),
    .row15(row15), .row16(row16), .row17(row17), .row18(row18), .row19(row19), .row20(row20), .row21(row21),
    .row22(row22), .row23(row23), .row24(row24), .row25(row25), .row26(row26), .row27(row27), .row28(row28),
    .row29(row29), .row30(row30), .row31(row31));

  // Notes on the sheet:
  //   Data
  //   contents of rom_1 (hex, n*v repeats v):
  //   d0 60 d1 ca a1 8c a1 d4
endmodule
